// Logisim project stack_logisim_normal.circ as structural Verilog: 18 circuits, main circuit DEMUX
module main (
  input  [1:0] COMMAND,
  input  RESET,
  input  CLK,
  input  [2:0] INDEX,
  input  [3:0] IO_DATA_in,
  output [3:0] IO_DATA_out
);

  stack stack_1 (
    .COMMAND(COMMAND), .RESET(RESET), .CLK(CLK), .INDEX(INDEX), .IO_DATA_in(IO_DATA_in),
    .IO_DATA_out(IO_DATA_out));
endmodule

module stack (
  input  [1:0] COMMAND,
  input  RESET,
  input  CLK,
  input  [2:0] INDEX,
  input  [3:0] IO_DATA_in,
  output [3:0] IO_DATA_out
);

  wire and_2_out, and_3_out, and_4_out, and_5_out, mem_1_q0, mem_1_q1, mem_1_q2, mem_1_q3, minusmod5_1_r0,
       minusmod5_1_r1, minusmod5_1_r2, not_1_out, not_2_out, not_3_out, not_4_out, optoinf_1_inf1,
       optoinf_1_inf2, or_1_out, or_2_out, or_3_out, or_4_out, or_5_out, plus1_1_b0, plus1_1_b1, plus1_1_b2,
       pointermanager_1_new0, pointermanager_1_new1, pointermanager_1_new2, pointermanager_1_saved0,
       pointermanager_1_saved1, pointermanager_1_saved2, por_1_out, threepusher_1_out0, threepusher_1_out1,
       threepusher_1_out2, threepusher_2_out0, threepusher_2_out1, threepusher_2_out2, threepusher_3_out0,
       threepusher_3_out1, threepusher_3_out2;

  POR por_1 (.out(por_1_out));
  or or_1 (or_1_out, por_1_out, RESET);
  not not_1 (not_1_out, COMMAND[0]);
  not not_2 (not_2_out, COMMAND[1]);
  not not_3 (not_3_out, COMMAND[1]);
  not not_4 (not_4_out, COMMAND[0]);
  // AND_Gate and_1 has open pins: in0=not_1_out, in1=not_2_out, out=open
  and and_2 (and_2_out, COMMAND[0], not_3_out);
  and and_3 (and_3_out, not_4_out, COMMAND[1]);
  and and_4 (and_4_out, COMMAND[0], COMMAND[1]);
  OpToInf optoinf_1 (.Op0(COMMAND[0]), .Op1(COMMAND[1]), .Inf1(optoinf_1_inf1), .Inf2(optoinf_1_inf2));
  or or_2 (or_2_out, and_3_out, and_4_out);
  and and_5 (and_5_out, CLK, or_2_out);
  Plus1 plus1_1 (.A0(INDEX[0]), .A1(INDEX[1]), .A2(INDEX[2]), .B0(plus1_1_b0), .B1(plus1_1_b1), .B2(plus1_1_b2));
  PointerManager pointermanager_1 (
    .inf1(optoinf_1_inf1), .inf2(optoinf_1_inf2), .reset(or_1_out), .C(CLK), .new0(pointermanager_1_new0),
    .saved0(pointermanager_1_saved0), .new1(pointermanager_1_new1), .saved1(pointermanager_1_saved1),
    .new2(pointermanager_1_new2), .saved2(pointermanager_1_saved2));
  // Probe on pointermanager_1_new0
  // Probe on pointermanager_1_new1
  // Probe on pointermanager_1_new2
  MinusMod5 minusmod5_1 (
    .A0(pointermanager_1_saved0), .A1(pointermanager_1_saved1), .A2(pointermanager_1_saved2),
    .B0(plus1_1_b0), .B1(plus1_1_b1), .B2(plus1_1_b2), .R0(minusmod5_1_r0), .R1(minusmod5_1_r1),
    .R2(minusmod5_1_r2));
  // Probe on pointermanager_1_saved0
  // Probe on pointermanager_1_saved1
  // Probe on pointermanager_1_saved2
  ThreePusher threepusher_1 (
    .In0(pointermanager_1_new0), .In1(pointermanager_1_new1), .In2(pointermanager_1_new2), .B(and_3_out),
    .Out0(threepusher_1_out0), .Out1(threepusher_1_out1), .Out2(threepusher_1_out2));
  ThreePusher threepusher_2 (
    .In0(minusmod5_1_r0), .In1(minusmod5_1_r1), .In2(minusmod5_1_r2), .B(and_4_out),
    .Out0(threepusher_2_out0), .Out1(threepusher_2_out1), .Out2(threepusher_2_out2));
  ThreePusher threepusher_3 (
    .In0(pointermanager_1_saved0), .In1(pointermanager_1_saved1), .In2(pointermanager_1_saved2),
    .B(and_2_out), .Out0(threepusher_3_out0), .Out1(threepusher_3_out1), .Out2(threepusher_3_out2));
  or or_3 (or_3_out, threepusher_3_out0, threepusher_1_out0, threepusher_2_out0);
  or or_4 (or_4_out, threepusher_3_out1, threepusher_1_out1, threepusher_2_out1);
  or or_5 (or_5_out, threepusher_3_out2, threepusher_1_out2, threepusher_2_out2);
  MEM mem_1 (
    .A0(or_3_out), .A1(or_4_out), .A2(or_5_out), .R_W(and_2_out), .C(CLK), .D0(IO_DATA_in[0]),
    .D1(IO_DATA_in[1]), .D2(IO_DATA_in[2]), .D3(IO_DATA_in[3]), .Reset(or_1_out), .Q0(mem_1_q0),
    .Q1(mem_1_q1), .Q2(mem_1_q2), .Q3(mem_1_q3));
  InAndOutHelper inandouthelper_1 (.A(and_5_out), .B(mem_1_q0), .Q(IO_DATA_in[0]));
  InAndOutHelper inandouthelper_2 (.A(and_5_out), .B(mem_1_q1), .Q(IO_DATA_in[1]));
  InAndOutHelper inandouthelper_3 (.A(and_5_out), .B(mem_1_q2), .Q(IO_DATA_in[2]));
  InAndOutHelper inandouthelper_4 (.A(and_5_out), .B(mem_1_q3), .Q(IO_DATA_in[3]));

  assign IO_DATA_out = IO_DATA_in;

  // Notes on the sheet:
  //   nop
  //   push
  //   pop
  //   get
  //   1, если надо читать
  //   новое значение
  //   pop
  //   push
  //   get
  //   сохранённое значение
  //   указателя
  //   в А0
  //   в А1
  //   в А2
  //   1, если надо читать
  //   0, если нет
endmodule

module InAndOutHelper (
  input  A,
  input  B,
  output Q
);

  wire not_1_out, not_2_out;

  not not_1 (not_1_out, B);
  not not_2 (not_2_out, A);
  Transistor transistor_1 (.in(A), .out(Q), .gate(not_1_out));
  // Probe on Q
  Transistor #(.\type ("n")) transistor_2 (.in(not_2_out), .out(Q), .gate(not_1_out));

  // Notes on the sheet:
  //   p
  //   n
endmodule

module OpToInf (
  input  Op0,
  input  Op1,
  output Inf1,
  output Inf2
);

  wire not_1_out, xor_1_out;

  xor xor_1 (xor_1_out, Op0, Op1);
  not not_1 (not_1_out, xor_1_out);
  or or_1 (Inf1, Op1, not_1_out);
  or or_2 (Inf2, not_1_out, Op0);
endmodule

module PointerManager (
  input  inf1,
  input  inf2,
  input  reset,
  input  C,
  output new0,
  output saved0,
  output new1,
  output saved1,
  output new2,
  output saved2
);

  wire and_1_out, and_2_out, not_1_out, not_2_out, or_1_out, or_2_out, pointermodifier_1_out_6,
       pointermodifier_1_out_7, pointermodifier_1_out_8;

  not not_1 (not_1_out, reset);
  or or_1 (or_1_out, reset, C);
  or or_2 (or_2_out, reset, not_2_out);
  not not_2 (not_2_out, C);
  and and_1 (and_1_out, inf1, not_1_out);
  and and_2 (and_2_out, inf2, not_1_out);
  PointerModifier pointermodifier_1 (
    .inf1(and_1_out), .inf2(and_2_out), .A0(saved0), .A1(saved1), .A2(saved2),
    .out_6(pointermodifier_1_out_6), .out_7(pointermodifier_1_out_7), .out_8(pointermodifier_1_out_8));
  Dtrigger dtrigger_1 (.C(or_1_out), .D(pointermodifier_1_out_6), .Q(new0));
  Dtrigger dtrigger_2 (.C(or_1_out), .D(pointermodifier_1_out_7), .Q(new1));
  Dtrigger dtrigger_3 (.C(or_1_out), .D(pointermodifier_1_out_8), .Q(new2));
  Dtrigger dtrigger_4 (.C(or_2_out), .D(new0), .Q(saved0));
  Dtrigger dtrigger_5 (.C(or_2_out), .D(new1), .Q(saved1));
  Dtrigger dtrigger_6 (.C(or_2_out), .D(new2), .Q(saved2));
endmodule

module PointerModifier (
  input  inf1,
  input  inf2,
  input  A0,
  input  A1,
  input  A2,
  output out_6,
  output out_7,
  output out_8
);

  wire and_1_out, and_2_out, and_3_out, and_4_out, and_5_out, and_6_out, and_7_out, and_8_out, and_9_out,
       and_10_out, and_11_out, and_12_out, minus1_1_b0, minus1_1_b1, minus1_1_b2, not_1_out, not_2_out,
       plus1_1_b0, plus1_1_b1, plus1_1_b2;

  not not_1 (not_1_out, inf1);
  not not_2 (not_2_out, inf2);
  and and_1 (and_1_out, not_1_out, inf2);
  and and_2 (and_2_out, inf1, not_2_out);
  and and_3 (and_3_out, inf1, inf2);
  Plus1 plus1_1 (.A0(A0), .A1(A1), .A2(A2), .B0(plus1_1_b0), .B1(plus1_1_b1), .B2(plus1_1_b2));
  Minus1 minus1_1 (.A0(A0), .A1(A1), .A2(A2), .B0(minus1_1_b0), .B1(minus1_1_b1), .B2(minus1_1_b2));
  and and_4 (and_4_out, and_1_out, plus1_1_b0);
  and and_5 (and_5_out, and_2_out, minus1_1_b0);
  and and_6 (and_6_out, and_3_out, A0);
  and and_7 (and_7_out, and_1_out, plus1_1_b1);
  and and_8 (and_8_out, and_2_out, minus1_1_b1);
  and and_9 (and_9_out, and_3_out, A1);
  and and_10 (and_10_out, and_1_out, plus1_1_b2);
  and and_11 (and_11_out, and_2_out, minus1_1_b2);
  and and_12 (and_12_out, and_3_out, A2);
  or or_1 (out_6, and_4_out, and_5_out, and_6_out);
  or or_2 (out_7, and_7_out, and_8_out, and_9_out);
  or or_3 (out_8, and_10_out, and_11_out, and_12_out);

  // Notes on the sheet:
  //   +
  //   --
  //   сохранение
endmodule

module MinusMod5 (
  input  A0,
  input  A1,
  input  A2,
  input  B0,
  input  B1,
  input  B2,
  output R0,
  output R1,
  output R2
);

  wire fivetothree_1_a0, fivetothree_1_a1, fivetothree_1_a2, minus1_1_b0, minus1_1_b1, minus1_1_b2,
       minus1_2_b0, minus1_2_b1, minus1_2_b2, minus1_3_b0, minus1_3_b1, minus1_3_b2, minus1_4_b0,
       minus1_4_b1, minus1_4_b2, threetofive_1_s0, threetofive_1_s1, threetofive_1_s2, threetofive_1_s3,
       threetofive_1_s4, threetofive_2_s0, threetofive_2_s1, threetofive_2_s2, threetofive_2_s3,
       threetofive_2_s4;

  ThreeToFive threetofive_1 (
    .A0(B0), .A1(B1), .A2(B2), .S0(threetofive_1_s0), .S1(threetofive_1_s1), .S2(threetofive_1_s2),
    .S3(threetofive_1_s3), .S4(threetofive_1_s4));
  ThreeToFive threetofive_2 (
    .A0(A0), .A1(A1), .A2(A2), .S0(threetofive_2_s0), .S1(threetofive_2_s1), .S2(threetofive_2_s2),
    .S3(threetofive_2_s3), .S4(threetofive_2_s4));
  FiveToThree fivetothree_1 (
    .S0(threetofive_2_s0), .S1(threetofive_2_s1), .S2(threetofive_2_s2), .S3(threetofive_2_s3),
    .S4(threetofive_2_s4), .A0(fivetothree_1_a0), .A1(fivetothree_1_a1), .A2(fivetothree_1_a2));
  Minus1 minus1_1 (
    .A0(fivetothree_1_a0), .A1(fivetothree_1_a1), .A2(fivetothree_1_a2), .B0(minus1_1_b0), .B1(minus1_1_b1),
    .B2(minus1_1_b2));
  Minus1 minus1_2 (
    .A0(minus1_1_b0), .A1(minus1_1_b1), .A2(minus1_1_b2), .B0(minus1_2_b0), .B1(minus1_2_b1), .B2(minus1_2_b2));
  Minus1 minus1_3 (
    .A0(minus1_2_b0), .A1(minus1_2_b1), .A2(minus1_2_b2), .B0(minus1_3_b0), .B1(minus1_3_b1), .B2(minus1_3_b2));
  Minus1 minus1_4 (
    .A0(minus1_3_b0), .A1(minus1_3_b1), .A2(minus1_3_b2), .B0(minus1_4_b0), .B1(minus1_4_b1), .B2(minus1_4_b2));
  Comp10to1 comp10to1_1 (
    .Bool0(threetofive_1_s0), .Bool1(threetofive_1_s1), .Bool2(threetofive_1_s2), .Bool3(threetofive_1_s3),
    .Bool4(threetofive_1_s4), .Value0(fivetothree_1_a0), .Value1(minus1_1_b0), .Value2(minus1_2_b0),
    .Value3(minus1_3_b0), .Value4(minus1_4_b0), .out_11(R0));
  Comp10to1 comp10to1_2 (
    .Bool0(threetofive_1_s0), .Bool1(threetofive_1_s1), .Bool2(threetofive_1_s2), .Bool3(threetofive_1_s3),
    .Bool4(threetofive_1_s4), .Value0(fivetothree_1_a1), .Value1(minus1_1_b1), .Value2(minus1_2_b1),
    .Value3(minus1_3_b1), .Value4(minus1_4_b1), .out_11(R1));
  Comp10to1 comp10to1_3 (
    .Bool0(threetofive_1_s0), .Bool1(threetofive_1_s1), .Bool2(threetofive_1_s2), .Bool3(threetofive_1_s3),
    .Bool4(threetofive_1_s4), .Value0(fivetothree_1_a2), .Value1(minus1_1_b2), .Value2(minus1_2_b2),
    .Value3(minus1_3_b2), .Value4(minus1_4_b2), .out_11(R2));

  // Notes on the sheet:
  //   преобразуем по модулю 5:
  //   иначе не меняет
  //   если А0, А1,А2 задавали число >= 5, то эта штука вычитает 5
endmodule

module Minus1 (
  input  A0,
  input  A1,
  input  A2,
  output B0,
  output B1,
  output B2
);

  wire threetofive_1_s0, threetofive_1_s1, threetofive_1_s2, threetofive_1_s3, threetofive_1_s4;

  ThreeToFive threetofive_1 (
    .A0(A0), .A1(A1), .A2(A2), .S0(threetofive_1_s0), .S1(threetofive_1_s1), .S2(threetofive_1_s2),
    .S3(threetofive_1_s3), .S4(threetofive_1_s4));
  FiveToThree fivetothree_1 (
    .S0(threetofive_1_s1), .S1(threetofive_1_s2), .S2(threetofive_1_s3), .S3(threetofive_1_s4),
    .S4(threetofive_1_s0), .A0(B0), .A1(B1), .A2(B2));
endmodule

module Plus1 (
  input  A0,
  input  A1,
  input  A2,
  output B0,
  output B1,
  output B2
);

  wire threetofive_1_s0, threetofive_1_s1, threetofive_1_s2, threetofive_1_s3, threetofive_1_s4;

  ThreeToFive threetofive_1 (
    .A0(A0), .A1(A1), .A2(A2), .S0(threetofive_1_s0), .S1(threetofive_1_s1), .S2(threetofive_1_s2),
    .S3(threetofive_1_s3), .S4(threetofive_1_s4));
  FiveToThree fivetothree_1 (
    .S0(threetofive_1_s4), .S1(threetofive_1_s0), .S2(threetofive_1_s1), .S3(threetofive_1_s2),
    .S4(threetofive_1_s3), .A0(B0), .A1(B1), .A2(B2));
endmodule

module MEM (
  input  A0,
  input  A1,
  input  A2,
  input  R_W,
  input  C,
  input  D0,
  input  D1,
  input  D2,
  input  D3,
  input  Reset,
  output Q0,
  output Q1,
  output Q2,
  output Q3
);

  wire and_1_out, demux_1_c0, demux_1_c1, demux_1_c2, demux_1_c3, demux_1_c4, stackcell_1_q0, stackcell_1_q1,
       stackcell_1_q2, stackcell_1_q3, stackcell_2_q0, stackcell_2_q1, stackcell_2_q2, stackcell_2_q3,
       stackcell_3_q0, stackcell_3_q1, stackcell_3_q2, stackcell_3_q3, stackcell_4_q0, stackcell_4_q1,
       stackcell_4_q2, stackcell_4_q3, stackcell_5_q0, stackcell_5_q1, stackcell_5_q2, stackcell_5_q3;

  and and_1 (and_1_out, R_W, C);
  DEMUX demux_1 (
    .A0(A0), .A1(A1), .A2(A2), .C(and_1_out), .C0(demux_1_c0), .C1(demux_1_c1), .C2(demux_1_c2),
    .C3(demux_1_c3), .C4(demux_1_c4));
  StackCell stackcell_1 (
    .Reset(Reset), .C(demux_1_c0), .D0(D0), .D1(D1), .D2(D2), .D3(D3), .Q0(stackcell_1_q0),
    .Q1(stackcell_1_q1), .Q2(stackcell_1_q2), .Q3(stackcell_1_q3));
  StackCell stackcell_2 (
    .Reset(Reset), .C(demux_1_c1), .D0(D0), .D1(D1), .D2(D2), .D3(D3), .Q0(stackcell_2_q0),
    .Q1(stackcell_2_q1), .Q2(stackcell_2_q2), .Q3(stackcell_2_q3));
  StackCell stackcell_3 (
    .Reset(Reset), .C(demux_1_c2), .D0(D0), .D1(D1), .D2(D2), .D3(D3), .Q0(stackcell_3_q0),
    .Q1(stackcell_3_q1), .Q2(stackcell_3_q2), .Q3(stackcell_3_q3));
  StackCell stackcell_4 (
    .Reset(Reset), .C(demux_1_c3), .D0(D0), .D1(D1), .D2(D2), .D3(D3), .Q0(stackcell_4_q0),
    .Q1(stackcell_4_q1), .Q2(stackcell_4_q2), .Q3(stackcell_4_q3));
  StackCell stackcell_5 (
    .Reset(Reset), .C(demux_1_c4), .D0(D0), .D1(D1), .D2(D2), .D3(D3), .Q0(stackcell_5_q0),
    .Q1(stackcell_5_q1), .Q2(stackcell_5_q2), .Q3(stackcell_5_q3));
  MUX mux_1 (
    .A0(A0), .A1(A1), .A2(A2), .D0(stackcell_1_q0), .D1(stackcell_1_q1), .D2(stackcell_1_q2),
    .D3(stackcell_1_q3), .D4(stackcell_2_q0), .D5(stackcell_2_q1), .D6(stackcell_2_q2), .D7(stackcell_2_q3),
    .D8(stackcell_3_q0), .D9(stackcell_3_q1), .D10(stackcell_3_q2), .D11(stackcell_3_q3),
    .D12(stackcell_4_q0), .D13(stackcell_4_q1), .D14(stackcell_4_q2), .D15(stackcell_4_q3),
    .D16(stackcell_5_q0), .D17(stackcell_5_q1), .D18(stackcell_5_q2), .D19(stackcell_5_q3), .Q0(Q0), .Q1(Q1),
    .Q2(Q2), .Q3(Q3));

  // Notes on the sheet:
  //   ячейка 0
  //   ячейка 1
  //   ячейка 2
  //   ячейка 3
  //   ячейка 4
endmodule

module DEMUX (
  input  A0,
  input  A1,
  input  A2,
  input  C,
  output C0,
  output C1,
  output C2,
  output C3,
  output C4
);

  wire threetofive_1_s0, threetofive_1_s1, threetofive_1_s2, threetofive_1_s3, threetofive_1_s4;

  ThreeToFive threetofive_1 (
    .A0(A0), .A1(A1), .A2(A2), .S0(threetofive_1_s0), .S1(threetofive_1_s1), .S2(threetofive_1_s2),
    .S3(threetofive_1_s3), .S4(threetofive_1_s4));
  and and_1 (C0, threetofive_1_s0, C);
  and and_2 (C1, threetofive_1_s1, C);
  and and_3 (C2, threetofive_1_s2, C);
  and and_4 (C3, threetofive_1_s3, C);
  and and_5 (C4, threetofive_1_s4, C);
endmodule

module MUX (
  input  A0,
  input  A1,
  input  A2,
  input  D0,
  input  D1,
  input  D2,
  input  D3,
  input  D4,
  input  D5,
  input  D6,
  input  D7,
  input  D8,
  input  D9,
  input  D10,
  input  D11,
  input  D12,
  input  D13,
  input  D14,
  input  D15,
  input  D16,
  input  D17,
  input  D18,
  input  D19,
  output Q0,
  output Q1,
  output Q2,
  output Q3
);

  wire and_1_out, and_2_out, and_3_out, and_4_out, and_5_out, and_6_out, and_7_out, and_8_out, and_9_out,
       and_10_out, and_11_out, and_12_out, and_13_out, and_14_out, and_15_out, and_16_out, and_17_out,
       and_18_out, and_19_out, and_20_out, threetofive_1_s0, threetofive_1_s1, threetofive_1_s2,
       threetofive_1_s3, threetofive_1_s4;

  ThreeToFive threetofive_1 (
    .A0(A0), .A1(A1), .A2(A2), .S0(threetofive_1_s0), .S1(threetofive_1_s1), .S2(threetofive_1_s2),
    .S3(threetofive_1_s3), .S4(threetofive_1_s4));
  and and_1 (and_1_out, threetofive_1_s0, D0);
  and and_2 (and_2_out, threetofive_1_s0, D1);
  and and_3 (and_3_out, threetofive_1_s0, D2);
  and and_4 (and_4_out, threetofive_1_s0, D3);
  and and_5 (and_5_out, threetofive_1_s1, D4);
  and and_6 (and_6_out, threetofive_1_s1, D5);
  and and_7 (and_7_out, threetofive_1_s1, D6);
  and and_8 (and_8_out, threetofive_1_s1, D7);
  and and_9 (and_9_out, threetofive_1_s2, D8);
  and and_10 (and_10_out, threetofive_1_s2, D9);
  and and_11 (and_11_out, threetofive_1_s2, D10);
  and and_12 (and_12_out, threetofive_1_s2, D11);
  and and_13 (and_13_out, threetofive_1_s3, D12);
  and and_14 (and_14_out, threetofive_1_s3, D13);
  and and_15 (and_15_out, threetofive_1_s3, D14);
  and and_16 (and_16_out, threetofive_1_s3, D15);
  and and_17 (and_17_out, threetofive_1_s4, D16);
  and and_18 (and_18_out, threetofive_1_s4, D17);
  and and_19 (and_19_out, threetofive_1_s4, D18);
  and and_20 (and_20_out, threetofive_1_s4, D19);
  or or_1 (Q0, and_1_out, and_5_out, and_9_out, and_13_out, and_17_out);
  or or_2 (Q1, and_2_out, and_6_out, and_10_out, and_14_out, and_18_out);
  or or_3 (Q2, and_3_out, and_7_out, and_11_out, and_15_out, and_19_out);
  or or_4 (Q3, and_4_out, and_8_out, and_12_out, and_16_out, and_20_out);
endmodule

module StackCell (
  input  Reset,
  input  C,
  input  D0,
  input  D1,
  input  D2,
  input  D3,
  output Q0,
  output Q1,
  output Q2,
  output Q3
);

  wire and_1_out, and_2_out, and_3_out, and_4_out, not_1_out, or_1_out;

  not not_1 (not_1_out, Reset);
  and and_1 (and_1_out, not_1_out, D0);
  and and_2 (and_2_out, not_1_out, D1);
  and and_3 (and_3_out, not_1_out, D2);
  and and_4 (and_4_out, not_1_out, D3);
  or or_1 (or_1_out, Reset, C);
  Dtrigger dtrigger_1 (.C(or_1_out), .D(and_1_out), .Q(Q0));
  Dtrigger dtrigger_2 (.C(or_1_out), .D(and_2_out), .Q(Q1));
  Dtrigger dtrigger_3 (.C(or_1_out), .D(and_3_out), .Q(Q2));
  Dtrigger dtrigger_4 (.C(or_1_out), .D(and_4_out), .Q(Q3));
endmodule

module Comp10to1 (
  input  Bool0,
  input  Bool1,
  input  Bool2,
  input  Bool3,
  input  Bool4,
  input  Value0,
  input  Value1,
  input  Value2,
  input  Value3,
  input  Value4,
  output out_11
);

  wire and_1_out, and_2_out, and_3_out, and_4_out, and_5_out;

  and and_1 (and_1_out, Bool0, Value0);
  and and_2 (and_2_out, Bool1, Value1);
  and and_3 (and_3_out, Bool2, Value2);
  and and_4 (and_4_out, Bool3, Value3);
  and and_5 (and_5_out, Bool4, Value4);
  or or_1 (out_11, and_1_out, and_2_out, and_3_out, and_4_out, and_5_out);
endmodule

module ThreePusher (
  input  In0,
  input  In1,
  input  In2,
  input  B,
  output Out0,
  output Out1,
  output Out2
);

  and AND0 (Out0, In0, B);
  and AND1 (Out1, In1, B);
  and AND2 (Out2, In2, B);
endmodule

module FiveToThree (
  input  S0,
  input  S1,
  input  S2,
  input  S3,
  input  S4,
  output A0,
  output A1,
  output A2
);

  or or_1 (A0, S1, S3);
  or or_2 (A1, S2, S3);

  assign A2 = S4;
endmodule

module ThreeToFive (
  input  A0,
  input  A1,
  input  A2,
  output S0,
  output S1,
  output S2,
  output S3,
  output S4
);

  wire and_1_out, and_2_out, and_3_out, and_6_out, and_7_out, and_8_out, not_1_out, not_2_out, not_3_out,
       not_4_out, not_5_out, not_6_out, not_7_out, not_8_out, not_9_out, not_10_out, not_11_out, not_12_out;

  not not_1 (not_1_out, A0);
  not not_2 (not_2_out, A1);
  not not_3 (not_3_out, A2);
  not not_4 (not_4_out, A1);
  not not_5 (not_5_out, A2);
  not not_6 (not_6_out, A0);
  not not_7 (not_7_out, A2);
  not not_8 (not_8_out, A2);
  not not_9 (not_9_out, A0);
  not not_10 (not_10_out, A1);
  not not_11 (not_11_out, A1);
  not not_12 (not_12_out, A0);
  and and_1 (and_1_out, not_1_out, not_2_out, not_3_out);
  and and_2 (and_2_out, A0, not_4_out, not_5_out);
  and and_3 (and_3_out, not_6_out, A1, not_7_out);
  and and_4 (S3, A0, A1, not_8_out);
  and and_5 (S4, not_9_out, not_10_out, A2);
  and and_6 (and_6_out, A0, not_11_out, A2);
  and and_7 (and_7_out, not_12_out, A1, A2);
  and and_8 (and_8_out, A0, A1, A2);
  or or_1 (S0, and_1_out, and_6_out);
  or or_2 (S1, and_2_out, and_7_out);
  or or_3 (S2, and_3_out, and_8_out);

  // Notes on the sheet:
  //   bit0
  //   bit1
  //   bit2
  //   0
  //   1
  //   2
  //   3
  //   4
  //   5
  //   6
  //   7
endmodule

module Dtrigger (
  input  C,
  input  D,
  output Q
);

  wire and_1_out, and_2_out, nor_2_out, not_1_out;

  not not_1 (not_1_out, D);
  and and_1 (and_1_out, not_1_out, C);
  and and_2 (and_2_out, C, D);
  nor nor_1 (Q, and_1_out, nor_2_out);
  nor nor_2 (nor_2_out, Q, and_2_out);
endmodule
